# Fritzing sketch skjema_planter1 (saved by Fritzing 0.9.3b)
breadboards: 1

parts:
  J1 = Basic Servo
  Part1 = Soil Moisture Sensor
  Raspberry_Pi_1 = Raspberry Pi 3 [part_number=RPI-3-V1.2]
  R1 = Resistor [tolerance=±5% resistance=330 package=THT]
  LED1 = LED - 5mm [color="Red (633nm)" package="5 mm [THT]"]

nets:
  GND: J1.gnd, Part1.GND, Raspberry_Pi_1.GND, LED1.cathode
  VCC: J1.vcc, Raspberry_Pi_1.5V
  N1: J1.pulse, Raspberry_Pi_1.GPIO18
  N2: Part1.SIG, Raspberry_Pi_1.GPIO21
  3V3: Part1.VCC, Raspberry_Pi_1.3v3, Raspberry_Pi_1.3V3
  N3: Raspberry_Pi_1.GPIO23, R1.Pin_1
  N4: R1.Pin_0, LED1.anode
